# Fritzing sketch circuit-design (saved by Fritzing 0.9.6b)
breadboards: 3

parts:
  U1 = NodeMCU V1.0
  S1 = Round Pushbutton
  S2 = Round Pushbutton
  S3 = Round Pushbutton
  R1 = Resistor [tolerance=±20% resistance=2.2k package="2512 [SMD]"]
  R2 = Resistor [tolerance=±20% resistance=2.2k package="2512 [SMD]"]
  R3 = Resistor [tolerance=±20% resistance=2.2k package="2512 [SMD]"]
  S4 = Round Pushbutton
  R4 = Resistor [tolerance=±20% resistance=2.2k package="2512 [SMD]"]
  S5 = Round Pushbutton
  R5 = Resistor [tolerance=±20% resistance=2.2k package="2512 [SMD]"]
  LED1 = smd LED [color="Red (633nm)" package="0603 [SMD]"]
  LED2 = smd LED [color="Green (555nm)" package="1206 [SMD]"]
  LED3 = smd LED [color="Blue (430nm)" package="1206 [SMD]"]
  LED4 = smd LED [color="White (8000K)" package="1206 [SMD]"]
  LED5 = smd LED [color="Orange (605nm)" package="1206 [SMD]"]
  R6 = Resistor [tolerance=±5% resistance=220 package="0603 [SMD]"]
  R7 = Resistor [tolerance=±5% resistance=220 package="0603 [SMD]"]
  R8 = Resistor [tolerance=±5% resistance=220 package="0603 [SMD]"]
  R9 = Resistor [tolerance=±5% resistance=220 package="0603 [SMD]"]
  R10 = Resistor [tolerance=±5% resistance=220 package="0603 [SMD]"]
  VCC1 = Battery
  VCC2 = Battery
  U2 = NodeMCU V1.0
  S6 = Round Pushbutton
  S7 = Round Pushbutton
  S8 = Round Pushbutton
  S9 = Round Pushbutton
  S10 = Round Pushbutton
  R11 = Resistor [tolerance=±20% resistance=2.2k package="2512 [SMD]"]
  R12 = Resistor [tolerance=±20% resistance=2.2k package="2512 [SMD]"]
  R13 = Resistor [tolerance=±20% resistance=2.2k package="2512 [SMD]"]
  R14 = Resistor [tolerance=±20% resistance=2.2k package="2512 [SMD]"]
  R15 = Resistor [tolerance=±20% resistance=2.2k package="2512 [SMD]"]
  LED6 = smd LED [color="Blue (430nm)" package="1206 [SMD]"]
  LED7 = smd LED [color="Green (555nm)" package="1206 [SMD]"]
  LED8 = smd LED [color="Orange (605nm)" package="1206 [SMD]"]
  LED9 = smd LED [color="White (8000K)" package="1206 [SMD]"]
  LED10 = smd LED [color="Red (633nm)" package="0603 [SMD]"]
  R16 = Resistor [tolerance=±5% resistance=220 package="0603 [SMD]"]
  R17 = Resistor [tolerance=±5% resistance=220 package="0603 [SMD]"]
  R18 = Resistor [tolerance=±5% resistance=220 package="0603 [SMD]"]
  R19 = Resistor [tolerance=±5% resistance=220 package="0603 [SMD]"]
  R20 = Resistor [tolerance=±5% resistance=220 package="0603 [SMD]"]

nets:
  N1: U1.D0, R6.Pin_1
  N2: U1.D1, R5.Pin_1
  N3: U1.D2, R3.Pin_1
  N4: U1.D3, R4.Pin_1
  N5: U1.D4, R7.Pin_0
  GND: U1.GND, VCC1.-, VCC2.-, U2.GND
  N6: U1.D5, R1.Pin_1
  N7: U1.D6, R8.Pin_0
  N8: U1.D7, R2.Pin_1
  N9: U1.D8, R9.Pin_0
  N10: U1.TX, R10.Pin_0
  VIN: U1.Vin, VCC1.+, VCC2.+, U2.Vin
  N11: U1.CMD, LED1.cathode, LED2.cathode, LED3.cathode, LED4.cathode, LED5.cathode
  N12: S1.leg0, S2.leg0, S3.leg0, R1.Pin_0, S4.leg0, S5.leg0
  N13: S1.leg1, R3.Pin_0
  N14: S2.leg1, R2.Pin_0
  N15: S4.leg1, R4.Pin_0
  N16: S5.leg1, R5.Pin_0
  N17: LED1.anode, R6.Pin_0
  N18: LED2.anode, R7.Pin_1
  N19: LED3.anode, R8.Pin_1
  N20: LED4.anode, R9.Pin_1
  N21: LED5.anode, R10.Pin_1
  N22: U2.D0, R19.Pin_1
  N23: U2.D1, R15.Pin_1
  N24: U2.D2, R11.Pin_1
  N25: U2.D3, R13.Pin_1
  N26: U2.D4, R17.Pin_0
  N27: U2.D5, R14.Pin_1
  N28: U2.D6, R16.Pin_0
  N29: U2.D7, R12.Pin_1
  N30: U2.D8, R20.Pin_0
  N31: U2.TX, R18.Pin_0
  N32: U2.CMD, LED6.cathode, LED7.cathode, LED8.cathode, LED9.cathode, LED10.cathode
  N33: S6.leg0, S7.leg0, S8.leg0, S9.leg0, S10.leg0, R14.Pin_0
  N34: S6.leg1, R13.Pin_0
  N35: S7.leg1, R11.Pin_0
  N36: S9.leg1, R12.Pin_0
  N37: S10.leg1, R15.Pin_0
  N38: LED6.anode, R16.Pin_1
  N39: LED7.anode, R17.Pin_1
  N40: LED8.anode, R18.Pin_1
  N41: LED9.anode, R20.Pin_1
  N42: LED10.anode, R19.Pin_0

custom parts:
  NodeMCU V1.0: ESP8266 based NodeMCU
